// Logisim project contador_assincrono_decre_modulo_8.circ as structural Verilog: 1 circuit, main circuit main
module main (
  input  in_1,
  input  in_2,
  output out_3,
  output out_4,
  output out_5
);

  J_K_Flip_Flop j_k_ff_1 (.J(in_1), .clk(in_2), .K(in_1), .Qn(out_5));  // open: Q, preset, en, reset
  J_K_Flip_Flop j_k_ff_2 (.J(in_1), .clk(out_5), .K(in_1), .Qn(out_4));  // open: Q, preset, en, reset
  J_K_Flip_Flop j_k_ff_3 (.J(in_1), .clk(out_4), .K(in_1), .Qn(out_3));  // open: Q, preset, en, reset
endmodule
