// Logisim project contador_modulo_13.circ as structural Verilog: 1 circuit, main circuit main
module main (
  input  in_1,
  input  in_2,
  output out_3,
  output out_4,
  output out_5,
  output out_6
);

  wire and_1_out, and_2_out, nand_1_out, not_1_out, not_2_out, not_3_out, not_4_out;

  J_K_Flip_Flop j_k_ff_1 (.J(in_1), .clk(in_2), .K(in_1), .Q(out_6), .reset(not_1_out));  // open: Qn, preset, en
  not not_1 (not_1_out, nand_1_out);
  J_K_Flip_Flop j_k_ff_2 (.J(out_6), .clk(in_2), .K(out_6), .Q(out_5), .reset(not_2_out));  // open: Qn, preset, en
  not not_2 (not_2_out, nand_1_out);
  and and_1 (and_1_out, out_5, out_6);
  J_K_Flip_Flop j_k_ff_3 (
    .J(and_1_out), .clk(in_2), .K(and_1_out), .Q(out_4), .reset(not_3_out));  // open: Qn, preset, en
  not not_3 (not_3_out, nand_1_out);
  and and_2 (and_2_out, out_4, and_1_out);
  J_K_Flip_Flop j_k_ff_4 (
    .J(and_2_out), .clk(in_2), .K(and_2_out), .Q(out_3), .reset(not_4_out));  // open: Qn, preset, en
  not not_4 (not_4_out, nand_1_out);
  nand nand_1 (nand_1_out, out_3, out_4, out_6);
endmodule
