// Logisim project contador_modulo_32.circ as structural Verilog: 2 circuits, main circuit main
module main (
  input  in_1,
  input  in_2,
  input  in_3,
  output out_4,
  output out_5,
  output out_6,
  output out_7,
  output out_8
);

  wire and_1_out, and_2_out, and_3_out;

  J_K_Flip_Flop j_k_ff_1 (.J(in_1), .clk(in_2), .K(in_1), .Q(out_5), .reset(in_3));  // open: Qn, preset, en
  and and_1 (and_1_out, out_5, out_6);
  J_K_Flip_Flop j_k_ff_2 (.J(out_5), .clk(in_2), .K(out_5), .Q(out_6), .reset(in_3));  // open: Qn, preset, en
  and and_2 (and_2_out, out_5, out_6, out_7);
  J_K_Flip_Flop j_k_ff_3 (.J(and_1_out), .clk(in_2), .K(and_1_out), .Q(out_7), .reset(in_3));  // open: Qn, preset, en
  J_K_Flip_Flop j_k_ff_4 (.J(and_2_out), .clk(in_2), .K(and_2_out), .Q(out_8), .reset(in_3));  // open: Qn, preset, en
  and and_3 (and_3_out, out_5, out_6, and_2_out, out_8);
  J_K_Flip_Flop j_k_ff_5 (.J(and_3_out), .clk(in_2), .K(and_3_out), .Q(out_4), .reset(in_3));  // open: Qn, preset, en
endmodule

module jk (
  input  in_1,
  input  in_2,
  input  in_3,
  output out_4,
  output out_5
);

  wire nand_1_out, nand_2_out;

  nand nand_1 (nand_1_out, in_2, in_3, out_4);
  nand nand_2 (nand_2_out, out_5, in_1, in_2);
  nor nor_1 (out_4, nand_2_out, out_5);
  nor nor_2 (out_5, out_4, nand_1_out);
endmodule
