// Logisim project contador_modulo_5_FF_T.circ as structural Verilog: 1 circuit, main circuit main
module main (
  input  in_1,
  input  in_2,
  output out_3,
  output out_4,
  output out_5
);

  wire and_1_out, nand_1_out, not_1_out, not_2_out, not_3_out;

  T_Flip_Flop t_ff_1 (.clk(in_2), .T(in_1), .Q(out_5), .reset(not_1_out));  // open: Qn, preset, en
  not not_1 (not_1_out, nand_1_out);
  T_Flip_Flop t_ff_2 (.clk(in_2), .T(out_5), .Q(out_4), .reset(not_2_out));  // open: Qn, preset, en
  not not_2 (not_2_out, nand_1_out);
  and and_1 (and_1_out, out_5, out_4);
  nand nand_1 (nand_1_out, out_3, out_5);
  T_Flip_Flop t_ff_3 (.clk(in_2), .T(and_1_out), .Q(out_3), .reset(not_3_out));  // open: Qn, preset, en
  not not_3 (not_3_out, nand_1_out);
endmodule
