// Logisim project contador_up_down_mod_16.circ as structural Verilog: 1 circuit, main circuit main
module main (
  input  in_1,
  input  in_2,
  input  in_3,
  output out_4,
  output DECRESCENTE,
  output out_6,
  output out_7,
  output out_8,
  output out_9,
  output out_10,
  output Q0
);

  wire and_1_out, and_2_out, and_3_out, and_4_out, and_5_out, and_6_out, not_1_out, not_2_out, not_3_out,
       not_4_out, not_5_out, or_1_out, or_2_out, or_3_out;

  not not_1 (not_1_out, in_1);
  and and_1 (and_1_out, in_1, Q0, out_9, out_10);
  and and_2 (and_2_out, DECRESCENTE, out_6, out_7, not_1_out);
  J_K_Flip_Flop j_k_ff_1 (
    .J(or_1_out), .clk(in_3), .K(or_1_out), .Q(out_8), .Qn(out_4), .reset(not_2_out));  // open: preset, en
  not not_2 (not_2_out, in_2);
  or or_1 (or_1_out, and_1_out, and_2_out);
  J_K_Flip_Flop j_k_ff_2 (
    .J(or_2_out), .clk(in_3), .K(or_2_out), .Q(out_9), .Qn(DECRESCENTE), .reset(not_3_out));  // open: preset, en
  not not_3 (not_3_out, in_2);
  and and_3 (and_3_out, in_1, out_10, Q0);
  and and_4 (and_4_out, out_7, out_6, not_1_out);
  or or_2 (or_2_out, and_3_out, and_4_out);
  J_K_Flip_Flop j_k_ff_3 (
    .J(or_3_out), .clk(in_3), .K(or_3_out), .Q(out_10), .Qn(out_6), .reset(not_4_out));  // open: preset, en
  not not_4 (not_4_out, in_2);
  and and_5 (and_5_out, in_1, Q0);
  or or_3 (or_3_out, and_5_out, and_6_out);
  and and_6 (and_6_out, out_7, not_1_out);
  J_K_Flip_Flop j_k_ff_4 (.J(in_2), .clk(in_3), .K(in_2), .Q(Q0), .Qn(out_7), .reset(not_5_out));  // open: preset, en
  not not_5 (not_5_out, in_2);

  // Notes on the sheet:
  //   CRESCENTE
  //   Q3'
  //   Q2'
  //   Q1'
  //   Q0'
  //   Q3
  //   Q2
  //   Q1
  //   D
  //   C
  //   B
endmodule
